// Logisim project Komparator_1-bitowy.circ as structural Verilog: 1 circuit, main circuit main
module main (
  input  A_i,
  input  B_i,
  input  A_i_1___B_i_1,
  output A_i_B_i,
  output A_i_b_i_2,
  output A_i_B_i_3
);

  wire nand_1_out, nand_2_out, nand_3_out, not_1_out, not_2_out;

  not not_1 (not_1_out, A_i);
  not not_2 (not_2_out, B_i);
  nand nand_1 (nand_1_out, not_2_out, A_i, A_i_1___B_i_1);
  nand nand_2 (nand_2_out, A_i_1___B_i_1, B_i, not_1_out);
  nand nand_3 (nand_3_out, nand_1_out, A_i_1___B_i_1, nand_2_out);
  not not_3 (A_i_B_i, nand_1_out);
  not not_4 (A_i_b_i_2, nand_3_out);
  not not_5 (A_i_B_i_3, nand_2_out);
endmodule
