// Logisim project Komparator_4-bitowy.circ as structural Verilog: 1 circuit, main circuit main
module main (
  input  A_3,
  input  A_2,
  input  A_1,
  input  A_0,
  input  B_3,
  input  B_2,
  input  B_1,
  input  B_0,
  input  _1,
  output A_B,
  output A_B_2,
  output A_B_3
);

  wire and_1_out, and_2_out, main_1_a_i_b_i, main_1_a_i_b_i_2, main_1_a_i_b_i_3, main_2_a_i_b_i,
       main_2_a_i_b_i_2, main_2_a_i_b_i_3, main_3_a_i_b_i, main_3_a_i_b_i_2, main_3_a_i_b_i_3,
       main_4_a_i_b_i, main_4_a_i_b_i_3;

  Komparator_1_bitowy_main main_1 (
    .A_i(A_3), .B_i(B_3), .A_i_1___B_i_1(_1), .A_i_B_i(main_1_a_i_b_i), .A_i_b_i_2(main_1_a_i_b_i_2),
    .A_i_B_i_3(main_1_a_i_b_i_3));
  Komparator_1_bitowy_main main_2 (
    .A_i(A_2), .B_i(B_2), .A_i_1___B_i_1(main_1_a_i_b_i_2), .A_i_B_i(main_2_a_i_b_i),
    .A_i_b_i_2(main_2_a_i_b_i_2), .A_i_B_i_3(main_2_a_i_b_i_3));
  Komparator_1_bitowy_main main_3 (
    .A_i(A_1), .B_i(B_1), .A_i_1___B_i_1(main_2_a_i_b_i_2), .A_i_B_i(main_3_a_i_b_i),
    .A_i_b_i_2(main_3_a_i_b_i_2), .A_i_B_i_3(main_3_a_i_b_i_3));
  Komparator_1_bitowy_main main_4 (
    .A_i(A_0), .B_i(B_0), .A_i_1___B_i_1(main_3_a_i_b_i_2), .A_i_B_i(main_4_a_i_b_i), .A_i_b_i_2(A_B_2),
    .A_i_B_i_3(main_4_a_i_b_i_3));
  and and_1 (and_1_out, ~main_1_a_i_b_i, ~main_2_a_i_b_i, ~main_3_a_i_b_i, ~main_4_a_i_b_i);  // AND_Gate
  and and_2 (and_2_out, ~main_4_a_i_b_i_3, ~main_3_a_i_b_i_3, ~main_2_a_i_b_i_3, ~main_1_a_i_b_i_3);  // AND_Gate
  not not_1 (A_B, and_1_out);
  not not_2 (A_B_3, and_2_out);
endmodule
