// Logisim project Licznik_punktow_compressed.circ as structural Verilog: 1 circuit, main circuit main
module main (
  input  x4,
  input  x3,
  input  x2,
  input  x1,
  input  inc_1,
  input  clock,
  input  in_7,
  output _7,
  output _7_2,
  output _6,
  output _7_3,
  output _6_2,
  output _5,
  output _6_3,
  output _5_2,
  output _4,
  output _5_3,
  output _4_2,
  output _3,
  output _4_3,
  output _3_2,
  output _2,
  output _3_3,
  output _2_2,
  output _1,
  output _2_3,
  output _1_2,
  output _0,
  output _1_3,
  output _0_2,
  output _0_3
);

  wire comparator_1_eq, comparator_2_eq, comparator_3_eq, or_1_out, or_2_out, or_3_out;
  wire [4:0] main_1_s0, main_2_s0, main_3_s0, register_1_q, register_2_q, register_3_q;

  Sumator_4_bitowy_main main_1 (
    .A1(x3), .A2(x2), .A3(x1), .B1(register_1_q[1]), .B2(register_1_q[2]), .B3(register_1_q[3]), .A0(x4),
    .B0(register_1_q[0]), ._0(inc_1), .S0(main_1_s0[0]), .S1(main_1_s0[1]), .S2(main_1_s0[2]),
    .S3(main_1_s0[3]), .S4(main_1_s0[4]));
  Register #(.width(5)) register_1 (.D(main_1_s0), .Q(register_1_q), .clk(clock), .clr(or_1_out));  // open: en
  ROM #(.addrWidth(5)) rom_1 (.addr(register_1_q), .data({_7, _6, _5, _4, _3, _2, _1, _0}));  // open: sel
  Sumator_4_bitowy_main main_2 (
    .A1(1'b0), .A2(1'b0), .A3(1'b0), .B1(register_2_q[1]), .B2(register_2_q[2]), .B3(register_2_q[3]),
    .A0(1'b0), .B0(register_2_q[0]), ._0(1'b1), .S0(main_2_s0[0]), .S1(main_2_s0[1]), .S2(main_2_s0[2]),
    .S3(main_2_s0[3]), .S4(main_2_s0[4]));
  or or_1 (or_1_out, in_7, comparator_1_eq);
  Comparator #(.mode("unsigned")) comparator_1 (
    .a({_7, _6, _5, _4, _3, _2, _1, _0}), .b({8{1'b0}}), .eq(comparator_1_eq));  // open: gt, lt
  Register #(.width(5)) register_2 (
    .D(main_2_s0), .Q(register_2_q), .clk(comparator_1_eq), .clr(or_2_out));  // open: en
  or or_2 (or_2_out, in_7, comparator_2_eq);
  ROM #(.addrWidth(5)) rom_2 (
    .addr(register_2_q), .data({_7_2, _6_2, _5_2, _4_2, _3_2, _2_2, _1_2, _0_2}));  // open: sel
  Comparator #(.mode("unsigned")) comparator_2 (
    .a({_7_2, _6_2, _5_2, _4_2, _3_2, _2_2, _1_2, _0_2}), .b({8{1'b0}}), .eq(comparator_2_eq));  // open: gt, lt
  Sumator_4_bitowy_main main_3 (
    .A1(1'b0), .A2(1'b0), .A3(1'b0), .B1(register_3_q[1]), .B2(register_3_q[2]), .B3(register_3_q[3]),
    .A0(1'b0), .B0(register_3_q[0]), ._0(1'b1), .S0(main_3_s0[0]), .S1(main_3_s0[1]), .S2(main_3_s0[2]),
    .S3(main_3_s0[3]), .S4(main_3_s0[4]));
  Register #(.width(5)) register_3 (
    .D(main_3_s0), .Q(register_3_q), .clk(comparator_2_eq), .clr(or_3_out));  // open: en
  ROM #(.addrWidth(5)) rom_3 (
    .addr(register_3_q), .data({_7_3, _6_3, _5_3, _4_3, _3_3, _2_3, _1_3, _0_3}));  // open: sel
  Comparator #(.mode("unsigned")) comparator_3 (
    .a({_7_3, _6_3, _5_3, _4_3, _3_3, _2_3, _1_3, _0_3}), .b({8{1'b0}}), .eq(comparator_3_eq));  // open: gt, lt
  or or_3 (or_3_out, comparator_3_eq, in_7);

  // Notes on the sheet:
  //   contents of rom_1 (hex, n*v repeats v):
  //   3f 6 5b 4f 66 6d 7d 7 7f 6f
  //   contents of rom_2 (hex, n*v repeats v):
  //   3f 6 5b 4f 66 6d 7d 7 7f 6f
  //   contents of rom_3 (hex, n*v repeats v):
  //   3f 6 5b 4f 66 6d 7d 7 7f 6f
endmodule
