// Logisim project Projekt.circ as structural Verilog: 1 circuit, main circuit main
module main (
  input  in_1,
  input  in_2,
  input  in_3,
  input  in_4,
  input  plus_1
);

  wire clock_1_out, main_1__0, main_1__0_2, main_1__0_3, main_1__1, main_1__1_2, main_1__1_3, main_1__2,
       main_1__2_2, main_1__2_3, main_1__3, main_1__3_2, main_1__3_3, main_1__4, main_1__4_2, main_1__4_3,
       main_1__5, main_1__5_2, main_1__5_3, main_1__6, main_1__6_2, main_1__6_3, main_1__7, main_1__7_2,
       main_1__7_3, Restart_out;

  Clock clock_1 (.out(clock_1_out));
  Licznik_punktow_compressed_main main_1 (
    .x4(in_1), .x3(in_2), .x2(in_3), .x1(in_4), .inc_1(plus_1), .clock(clock_1_out), ._0_3(main_1__0_3),
    ._1_3(main_1__1_3), ._2_3(main_1__2_3), ._3_3(main_1__3_3), ._4_3(main_1__4_3), ._5_3(main_1__5_3),
    ._6_3(main_1__6_3), ._7_3(main_1__7_3), ._7_2(main_1__7_2), ._6_2(main_1__6_2), ._5_2(main_1__5_2),
    ._4_2(main_1__4_2), ._3_2(main_1__3_2), ._2_2(main_1__2_2), ._1_2(main_1__1_2), ._0_2(main_1__0_2),
    ._7(main_1__7), ._6(main_1__6), ._5(main_1__5), ._4(main_1__4), ._3(main_1__3), ._2(main_1__2),
    ._1(main_1__1), ._0(main_1__0), .in_7(Restart_out));
  Button Restart (.out(Restart_out));
  _7_Segment_Display u_7_segment_display_1 (
    .g(main_1__6_3), .f(main_1__5_3), .a(main_1__0_3), .b(main_1__1_3), .e(main_1__4_3), .d(main_1__3_3),
    .c(main_1__2_3), .dp(main_1__7_3));
  _7_Segment_Display u_7_segment_display_2 (
    .g(main_1__6), .f(main_1__5), .a(main_1__0), .b(main_1__1), .e(main_1__4), .d(main_1__3), .c(main_1__2),
    .dp(main_1__7));
  _7_Segment_Display u_7_segment_display_3 (
    .g(main_1__6_2), .f(main_1__5_2), .a(main_1__0_2), .b(main_1__1_2), .e(main_1__4_2), .d(main_1__3_2),
    .c(main_1__2_2), .dp(main_1__7_2));

  // Notes on the sheet:
  //   1
  //   5
  //   6
  //   0
  //   7
  //   2
  //   3
  //   4
  //   5
  //   0
  //   1
  //   1
  //   5
  //   6
  //   6
  //   0
  //   7
  //   7
  //   2
  //   2
  //   3
  //   3
  //   4
  //   4
endmodule
