// Logisim project Sumator_1-bitowy.circ as structural Verilog: 1 circuit, main circuit main
module main (
  input  A,
  input  B,
  input  C_in,
  output S,
  output Cout
);

  wire nand_1_out, nand_2_out, nand_3_out, xor_1_out;

  xor xor_1 (xor_1_out, A, B);
  xor xor_2 (S, xor_1_out, C_in);
  nand nand_1 (nand_1_out, C_in, B);
  nand nand_2 (nand_2_out, A, C_in);
  nand nand_3 (nand_3_out, B, A);
  nand nand_4 (Cout, nand_1_out, nand_2_out, nand_3_out);
endmodule
