// Logisim project Sumator_4-bitowy.circ as structural Verilog: 1 circuit, main circuit main
module main (
  input  A1,
  input  A2,
  input  A3,
  input  B1,
  input  B2,
  input  B3,
  input  A0,
  input  B0,
  input  _0,
  output S0,
  output S1,
  output S2,
  output S3,
  output S4
);

  wire main_1_cout, main_2_cout, main_3_cout;

  Sumator_1_bitowy_main main_1 (.A(A0), .B(B0), .C_in(_0), .S(S0), .Cout(main_1_cout));
  Sumator_1_bitowy_main main_2 (.A(A1), .B(B1), .C_in(main_1_cout), .S(S1), .Cout(main_2_cout));
  Sumator_1_bitowy_main main_3 (.A(A2), .B(B2), .C_in(main_2_cout), .S(S2), .Cout(main_3_cout));
  Sumator_1_bitowy_main main_4 (.A(A3), .B(B3), .C_in(main_3_cout), .S(S3), .Cout(S4));
endmodule
