// Logisim project U2_wyswietlacz.circ as structural Verilog: 1 circuit, main circuit main
module main (
  input  A3,
  input  A2,
  input  A1,
  input  A0,
  input  B3,
  input  B2,
  input  B1,
  input  B0,
  input  in_9,
  input  [4:0] in_10,
  input  [4:0] in_11,
  input  [4:0] in_12,
  input  [4:0] in_13,
  input  [4:0] in_14
);

  wire [2:0] main_1_a_b_3;
  wire [24:0] rom_1_data;

  Komparator_4_bitowy_main main_1 (
    .A_3(A3), .A_2(A2), .A_1(A1), .A_0(A0), .B_3(B3), .B_2(B2), .B_1(B1), .B_0(B0), ._1(in_9),
    .A_B(main_1_a_b_3[2]), .A_B_2(main_1_a_b_3[1]), .A_B_3(main_1_a_b_3[0]));
  ROM #(.addrWidth(3), .dataWidth(25)) rom_1 (.addr(main_1_a_b_3), .data(rom_1_data));  // open: sel
  DotMatrix #(.inputtype("row"), .matrixrows(5)) dotmatrix_1 (
    .row0(rom_1_data[24:20]), .row1(rom_1_data[19:15]), .row2(rom_1_data[14:10]), .row3(rom_1_data[9:5]),
    .row4(rom_1_data[4:0]));
  DotMatrix #(.inputtype("row"), .matrixrows(5)) dotmatrix_2 (
    .row0(in_10), .row1(in_11), .row2(in_12), .row3(in_13), .row4(in_14));

  // Notes on the sheet:
  //   contents of rom_1 (hex, n*v repeats v):
  //   477dc4 1555555 701c0 0 820888
endmodule
