// Logisim project U_3_TB.circ as structural Verilog: 1 circuit, main circuit main
module main (
  input  x1,
  input  x2,
  input  x3,
  input  x4,
  input  c_in
);

  wire clock_1_out;
  wire [4:0] main_1_s0, register_1_q;
  wire [7:0] rom_1_data, rom_1_data_2;

  _7_Segment_Display u_7_segment_display_1 (
    .g(rom_1_data_2[6]), .f(rom_1_data_2[5]), .a(rom_1_data_2[0]), .b(rom_1_data_2[1]), .e(rom_1_data_2[4]),
    .d(rom_1_data_2[3]), .c(rom_1_data_2[2]), .dp(rom_1_data_2[7]));
  Sumator_4_bitowy_main main_1 (
    .A1(x2), .A2(x3), .A3(x4), .B1(register_1_q[1]), .B2(register_1_q[2]), .B3(register_1_q[3]), .A0(x1),
    .B0(register_1_q[0]), ._0(c_in), .S0(main_1_s0[0]), .S1(main_1_s0[1]), .S2(main_1_s0[2]),
    .S3(main_1_s0[3]), .S4(main_1_s0[4]));
  Clock clock_1 (.out(clock_1_out));
  Register #(.width(5)) register_1 (.D(main_1_s0), .Q(register_1_q), .clk(clock_1_out));  // open: en, clr
  _7_Segment_Display u_7_segment_display_2 (
    .g(rom_1_data[6]), .f(rom_1_data[5]), .a(rom_1_data[0]), .b(rom_1_data[1]), .e(rom_1_data[4]),
    .d(rom_1_data[3]), .c(rom_1_data[2]), .dp(rom_1_data[7]));
  ROM #(.addrWidth(5), .dataWidth(16)) rom_1 (.addr(register_1_q), .data({rom_1_data_2, rom_1_data}));  // open: sel

  // Notes on the sheet:
  //   contents of rom_1 (hex, n*v repeats v):
  //   3f 6 5b 4f 66 6d 7d 7 7f 6f 63f 606 65b 64f 666 66d 67d
endmodule
