// Logisim project and_or_led_kodowanie_znakow.circ as structural Verilog: 1 circuit, main circuit main
module main (
  input  [1:0] in_1,
  input  [4:0] in_2,
  input  [4:0] in_3,
  input  [4:0] in_4,
  input  [4:0] in_5,
  input  [4:0] in_6,
  input  [4:0] in_7,
  input  [4:0] in_8,
  input  [4:0] in_9,
  input  [4:0] in_10,
  input  [4:0] in_11
);

  wire [24:0] and_1_out, multiplexer_1_out, or_1_out;

  assign or_1_out = 25'h14a729c | 25'h7294a5;  // OR_Gate or_1, 25 bits wide
  assign and_1_out = 25'h14a729c & 25'h7294a5;  // AND_Gate and_1, 25 bits wide
  Multiplexer #(.select(2), .width(25), .disabled(0), .enable("false")) multiplexer_1 (
    .in0(25'h14a729c), .in1(25'h7294a5), .in2(or_1_out), .in3(and_1_out), .out(multiplexer_1_out), .sel(in_1));
  DotMatrix #(.inputtype("row"), .matrixrows(5)) dotmatrix_1 (
    .row0(multiplexer_1_out[4:0]), .row1(multiplexer_1_out[9:5]), .row2(multiplexer_1_out[14:10]),
    .row3(multiplexer_1_out[19:15]), .row4(multiplexer_1_out[24:20]));
  DotMatrix #(.inputtype("row"), .matrixrows(5)) dotmatrix_2 (
    .row0(in_2), .row1(in_3), .row2(in_4), .row3(in_5), .row4(in_6));
  DotMatrix #(.inputtype("row"), .matrixrows(5)) dotmatrix_3 (
    .row0(in_7), .row1(in_8), .row2(in_9), .row3(in_10), .row4(in_11));

  // Notes on the sheet:
  //   Kwadrat
  //   Krzyżyk
  //   00 - kwadrat
  //   01 - krzyżyk
  //   10 - kwadrat i krzyżyk
  //   11 - część wspólna
endmodule
