// Logisim project keyboard_dziala_wyswietlacz.circ as structural Verilog: 1 circuit, main circuit main
module main (
);

  wire comparator_1_eq, comparator_2_eq, comparator_3_eq, comparator_4_eq, comparator_5_eq, comparator_6_eq,
       comparator_7_eq, controlled_buffer_1_out, keyboard_1_avail, \Zegar_taktujący_out ;
  wire [2:0] counter_1_q;
  wire [4:0] register_2_q, register_2_q_2, register_2_q_3, register_2_q_4, register_2_q_5, register_3_q,
       register_3_q_2, register_3_q_3, register_3_q_4, register_3_q_5, register_4_q, register_4_q_2,
       register_4_q_3, register_4_q_4, register_4_q_5, register_5_q, register_5_q_2, register_5_q_3,
       register_5_q_4, register_5_q_5, register_7_q, register_7_q_2, register_7_q_3, register_7_q_4,
       register_7_q_5;
  wire [6:0] demultiplexer_1_out0, demultiplexer_1_out1, demultiplexer_1_out2, demultiplexer_1_out3,
       demultiplexer_1_out4, demultiplexer_1_out5, keyboard_1_data, register_1_q;
  wire [24:0] register_6_q, rom_2_data, rom_3_data, rom_4_data, rom_5_data, rom_6_data, rom_7_data;

  Clock \Zegar_taktujący  (.out(\Zegar_taktujący_out ));
  assign controlled_buffer_1_out = keyboard_1_avail ? \Zegar_taktujący_out  : 1'bz;  // Controlled_Buffer controlled_buffer_1
  Pull_Resistor pull_resistor_1 (.node(controlled_buffer_1_out));
  Keyboard keyboard_1 (
    .clk(controlled_buffer_1_out), .re(1'b1), .avail(keyboard_1_avail), .data(keyboard_1_data));  // open: clr
  Demultiplexer #(.select(3), .width(7)) demultiplexer_1 (
    .out0(demultiplexer_1_out0), .out1(demultiplexer_1_out1), .out2(demultiplexer_1_out2),
    .out3(demultiplexer_1_out3), .out4(demultiplexer_1_out4), .out5(demultiplexer_1_out5), .in(register_1_q),
    .sel(counter_1_q));  // open: out6, out7, en
  Register #(.width(7)) register_1 (
    .D(keyboard_1_data), .Q(register_1_q), .clk(controlled_buffer_1_out));  // open: en, clr
  ROM #(.addrWidth(3), .dataWidth(5)) rom_1 ();  // open: addr, data, sel
  Counter #(.width(3), .max('h6)) counter_1 (
    .Q(counter_1_q), .clk(keyboard_1_avail));  // open: load, D, count, carry, clr
  ROM #(.addrWidth(7), .dataWidth(25)) rom_2 (.addr(demultiplexer_1_out0), .data(rom_2_data));  // open: sel
  ROM #(.addrWidth(7), .dataWidth(25)) rom_3 (.addr(demultiplexer_1_out1), .data(rom_3_data));  // open: sel
  ROM #(.addrWidth(7), .dataWidth(25)) rom_4 (.addr(demultiplexer_1_out2), .data(rom_4_data));  // open: sel
  ROM #(.addrWidth(7), .dataWidth(25)) rom_5 (.addr(demultiplexer_1_out3), .data(rom_5_data));  // open: sel
  ROM #(.addrWidth(7), .dataWidth(25)) rom_6 (.addr(demultiplexer_1_out4), .data(rom_6_data));  // open: sel
  ROM #(.addrWidth(7), .dataWidth(25)) rom_7 (.addr(demultiplexer_1_out5), .data(rom_7_data));  // open: sel
  Comparator #(.width(3)) comparator_1 (.a(counter_1_q), .b(3'b000), .eq(comparator_1_eq));  // open: gt, lt
  Comparator #(.width(3)) comparator_2 (.a(counter_1_q), .b(3'b001), .eq(comparator_2_eq));  // open: gt, lt
  Comparator #(.width(3)) comparator_3 (.a(counter_1_q), .b(3'b010), .eq(comparator_3_eq));  // open: gt, lt
  Comparator #(.width(3)) comparator_4 (.a(counter_1_q), .b(3'b011), .eq(comparator_4_eq));  // open: gt, lt
  Comparator #(.width(3)) comparator_5 (.a(counter_1_q), .b(3'b100), .eq(comparator_5_eq));  // open: gt, lt
  Comparator #(.width(3)) comparator_6 (.a(counter_1_q), .b(3'b101), .eq(comparator_6_eq));  // open: gt, lt
  Comparator #(.width(3)) comparator_7 (.a(counter_1_q), .b(3'b110), .eq(comparator_7_eq));  // open: gt, lt
  Register #(.width(25)) register_2 (
    .D(rom_2_data), .en(comparator_1_eq),
    .Q({register_2_q_5, register_2_q_4, register_2_q_3, register_2_q_2, register_2_q}),
    .clk(\Zegar_taktujący_out ), .clr(comparator_7_eq));
  Register #(.width(25)) register_3 (
    .D(rom_3_data), .en(comparator_2_eq),
    .Q({register_3_q_5, register_3_q_4, register_3_q_3, register_3_q_2, register_3_q}),
    .clk(\Zegar_taktujący_out ), .clr(comparator_7_eq));
  Register #(.width(25)) register_4 (
    .D(rom_4_data), .en(comparator_3_eq),
    .Q({register_4_q_5, register_4_q_4, register_4_q_3, register_4_q_2, register_4_q}),
    .clk(\Zegar_taktujący_out ), .clr(comparator_7_eq));
  Register #(.width(25)) register_5 (
    .D(rom_6_data), .en(comparator_5_eq),
    .Q({register_5_q_5, register_5_q_4, register_5_q_3, register_5_q_2, register_5_q}),
    .clk(\Zegar_taktujący_out ), .clr(comparator_7_eq));
  DotMatrix #(.matrixcols(30), .matrixrows(5)) dotmatrix_1 (
    .col0(register_2_q_5), .col1(register_2_q_4), .col2(register_2_q_3), .col3(register_2_q_2),
    .col4(register_2_q), .col5(register_3_q_5), .col6(register_3_q_4), .col7(register_3_q_3),
    .col8(register_3_q_2), .col9(register_3_q), .col10(register_4_q_5), .col11(register_4_q_4),
    .col12(register_4_q_3), .col13(register_4_q_2), .col14(register_4_q), .col15(register_6_q[24:20]),
    .col16(register_6_q[19:15]), .col17(register_6_q[14:10]), .col18(register_6_q[9:5]),
    .col19(register_6_q[4:0]), .col20(register_5_q_5), .col21(register_5_q_4), .col22(register_5_q_3),
    .col23(register_5_q_2), .col24(register_5_q), .col25(register_7_q_5), .col26(register_7_q_4),
    .col27(register_7_q_3), .col28(register_7_q_2), .col29(register_7_q));
  Register #(.width(25)) register_6 (
    .D(rom_5_data), .en(comparator_4_eq), .Q(register_6_q), .clk(\Zegar_taktujący_out ), .clr(comparator_7_eq));
  Register #(.width(25)) register_7 (
    .D(rom_7_data), .en(comparator_6_eq),
    .Q({register_7_q_5, register_7_q_4, register_7_q_3, register_7_q_2, register_7_q}),
    .clk(\Zegar_taktujący_out ), .clr(comparator_7_eq));

  // Notes on the sheet:
  //   contents of rom_2 (hex, n*v repeats v):
  //   729ca5 96*0 fa3c00 1faa800 e8a800 1f8b800 1fad400 1fa5000 1f8dc00 1f27c00 7c00 20f800 1f22a20
  //   1f08400 1f4111f 1f4105f e8b800 1fa2000 0 1fa2c00 9ac800 10fc000 1e0f800 0 1e0983e 1151151 183e000
  //   13ae400
  //   contents of rom_3 (hex, n*v repeats v):
  //   97*0 fa3c00 1faa800 e8a800 1f8b800 1fad400 1fa5000 1f8dc00 1f27c00 7c00 20f800 1f22a20 1f08400
  //   1f4111f 1f4105f e8b800 1fa2000 0 1fa2c00 9ac800 10fc000 1e0f800 0 1e0983e 1151151 183e000 13ae400
  //   contents of rom_4 (hex, n*v repeats v):
  //   97*0 fa3c00 1faa800 e8a800 1f8b800 1fad400 1fa5000 1f8dc00 1f27c00 7c00 20f800 1f22a20 1f08400
  //   1f4111f 1f4105f e8b800 1fa2000 0 1fa2c00 9ac800 10fc000 1e0f800 0 1e0983e 1151151 183e000 13ae400
  //   contents of rom_5 (hex, n*v repeats v):
  //   97*0 fa3c00 1faa800 e8a800 1f8b800 1fad400 1fa5000 1f8dc00 1f27c00 7c00 20f800 1f22a20 1f08400
  //   1f4111f 1f4105f e8b800 1fa2000 0 1fa2c00 9ac800 10fc000 1e0f800 0 1e0983e 1151151 183e000 13ae400
  //   contents of rom_6 (hex, n*v repeats v):
  //   97*0 fa3c00 1faa800 e8a800 1f8b800 1fad400 1fa5000 1f8dc00 1f27c00 7c00 20f800 1f22a20 1f08400
  //   1f4111f 1f4105f e8b800 1fa2000 0 1fa2c00 9ac800 10fc000 1e0f800 0 1e0983e 1151151 183e000 13ae400
  //   contents of rom_7 (hex, n*v repeats v):
  //   97*0 fa3c00 1faa800 e8a800 1f8b800 1fad400 1fa5000 1f8dc00 1f27c00 7c00 20f800 1f22a20 1f08400
  //   1f4111f 1f4105f e8b800 1fa2000 0 1fa2c00 9ac800 10fc000 1e0f800 0 1e0983e 1151151 183e000 13ae400
endmodule
