// Logisim project program_wyczyszyczony.circ as structural Verilog: 1 circuit, main circuit main
module main (
);

  wire and_1_out, clock_ekran, comparator_3_eq, comparator_4_eq, comparator_5_eq, comparator_6_eq,
       comparator_7_eq, comparator_8_eq, comparator_9_eq, comparator_10_eq, comparator_11_eq,
       comparator_12_eq, comparator_13_eq, comparator_14_eq, comparator_15_eq, comparator_16_eq,
       comparator_17_eq, comparator_18_eq, keyboard_1_avail, komp_lewo, komp_prawo, not_1_out, not_2_out,
       not_3_out, or_1_out, or_6_out, or_7_out, pull_resistor_1_node, res_l, res_p, rgb_video_1_p1,
       syg_licz_l, syg_licz_p, zegar;
  wire [2:0] multiplexer_1_out;
  wire [4:0] adder_1_out, adder_4_out, adder_5_out, adder_6_out, adder_7_out, adder_8_out, adder_9_out,
       adder_10_out, adder_11_out, adder_12_out, counter_2_q, counter_3_q, counter_4_q, counter_5_q,
       counter_6_q, counter_7_q, counter_8_q, counter_9_q, counter_10_q, or_2_out, or_3_out, skrajny_lewo,
       skrajny_prawo, subtractor_1_out, subtractor_2_out, subtractor_3_out, subtractor_4_out,
       subtractor_5_out, wsp_x, wsp_y;
  wire [6:0] keyboard_1_data, register_1_q;
  wire [9:0] counter_1_q;
  wire [15:0] controlled_buffer_2_out, or_5_out, rgb_video_1_p5, rom_1_data, undriven;

  Clock clock_1 (.out(zegar));
  Adder #(.width(5)) adder_1 (.a(counter_2_q), .b(5'b00100), .out(adder_1_out));  // open: cin, cout
  Subtractor #(.width(5)) subtractor_1 (.a(counter_3_q), .b(5'b00100), .out(subtractor_1_out));  // open: bin, bout
  Counter #(.max('h3ff), .width(10)) counter_1 (
    .count(zegar), .Q(counter_1_q), .clk(zegar));  // open: load, D, carry, up, clr
  Pull_Resistor pull_resistor_1 (.node(pull_resistor_1_node));
  assign pull_resistor_1_node = keyboard_1_avail ? zegar : 1'bz;  // Controlled_Buffer controlled_buffer_1
  Keyboard #(.buflen(1)) keyboard_1 (
    .clk(pull_resistor_1_node), .re(1'b1), .avail(keyboard_1_avail), .data(keyboard_1_data));  // open: clr
  Counter #(.max('h1f), .width(5)) counter_2 (
    .load(syg_licz_p), .D(adder_1_out), .count(not_1_out), .Q(counter_2_q), .clk(syg_licz_p));  // open: carry, up, clr
  Counter #(.max('h1f), .width(5)) counter_3 (
    .load(syg_licz_l), .D(subtractor_1_out), .count(not_2_out), .Q(counter_3_q), .clk(syg_licz_l));  // open: carry, up, clr
  not not_1 (not_1_out, syg_licz_p);
  not not_2 (not_2_out, syg_licz_l);
  Adder #(.width(5)) adder_2 (.a(counter_2_q), .b(counter_3_q), .out(skrajny_lewo));  // open: cin, cout
  Counter #(.max('h1f), .width(5)) counter_4 (
    .count(zegar), .Q(counter_4_q), .clk(zegar));  // open: load, D, carry, up, clr
  Adder #(.width(5)) adder_3 (.a(skrajny_lewo), .b(5'b00100), .out(skrajny_prawo));  // open: cin, cout
  Register #(.width(7)) register_1 (
    .D(keyboard_1_data), .Q(register_1_q), .clk(keyboard_1_avail), .clr(or_1_out));  // open: en
  // Probe on skrajny_prawo
  or or_1 (or_1_out, syg_licz_p, syg_licz_l);
  Comparator #(.width(5)) comparator_1 (.a(skrajny_lewo), .b({5{1'b0}}), .eq(komp_lewo));  // open: gt, lt
  Comparator #(.width(5)) comparator_2 (.a(skrajny_prawo), .b({5{1'b0}}), .eq(komp_prawo));  // open: gt, lt
  // Probe on skrajny_lewo
  // Probe on skrajny_prawo
  Adder #(.width(5)) adder_4 (.a(counter_5_q), .b(5'b00100), .out(adder_4_out));  // open: cin, cout
  Adder #(.width(5)) adder_5 (.a(counter_6_q), .b(5'b00100), .out(adder_5_out));  // open: cin, cout
  Adder #(.width(5)) adder_6 (.a(counter_7_q), .b(5'b00100), .out(adder_6_out));  // open: cin, cout
  Comparator #(.width(7)) comparator_3 (.a(register_1_q), .b(7'b1100001), .eq(comparator_3_eq));  // open: gt, lt
  Comparator #(.width(7)) comparator_4 (.a(register_1_q), .b(7'b1100100), .eq(comparator_4_eq));  // open: gt, lt
  Comparator #(.width(7)) comparator_5 (.a(register_1_q), .b(7'b1100001), .eq(comparator_5_eq));  // open: gt, lt
  Comparator #(.width(7)) comparator_6 (.a(register_1_q), .b(7'b1100100), .eq(comparator_6_eq));  // open: gt, lt
  Adder #(.width(5)) adder_7 (.a(counter_8_q), .b(5'b00100), .out(adder_7_out));  // open: cin, cout
  Adder #(.width(5)) adder_8 (.a(5'b00100), .b(counter_9_q), .out(adder_8_out));  // open: cin, cout
  Comparator #(.width(5)) comparator_7 (.a(counter_4_q), .b({5{1'b1}}), .eq(comparator_7_eq));  // open: gt, lt
  Counter #(.max('h1f), .width(5)) counter_5 (
    .load(1'b1), .D(adder_4_out), .count(1'b0), .Q(counter_5_q), .clk(syg_licz_l));  // open: carry, up, clr
  Counter #(.max('h1f), .width(5)) counter_6 (
    .load(1'b1), .D(adder_5_out), .count(1'b0), .Q(counter_6_q), .clk(syg_licz_l));  // open: carry, up, clr
  Counter #(.max('h1f), .width(5)) counter_7 (
    .load(1'b1), .D(adder_6_out), .count(1'b0), .Q(counter_7_q), .clk(syg_licz_l));  // open: carry, up, clr
  // bufor_fixed bufor_fixed_1: pin names not known; wires that end beside it: comparator_3_eq, komp_lewo, syg_licz_l
  // bufor_fixed bufor_fixed_2: pin names not known; wires that end beside it: comparator_4_eq, komp_prawo, syg_licz_p
  // bufor_fixed bufor_fixed_3: pin names not known; wires that end beside it: comparator_5_eq, komp_lewo, res_l
  // bufor_fixed bufor_fixed_4: pin names not known; wires that end beside it: 7'b1100100, 7'b1100001, comparator_6_eq, komp_prawo, res_p
  Counter #(.max('h1f), .width(5)) counter_8 (
    .load(1'b1), .D(adder_7_out), .count(1'b0), .Q(counter_8_q), .clk(res_p));  // open: carry, up, clr
  Counter #(.max('h1f), .width(5)) counter_9 (
    .load(1'b1), .D(adder_8_out), .count(1'b0), .Q(counter_9_q), .clk(res_l));  // open: carry, up, clr
  Multiplexer #(.select(5), .width(3)) multiplexer_1 (
    .in0(3'b111), .in3(3'b000), .in8(3'b001), .in12(3'b010), .in16(3'b011), .in20(3'b100), .in24(3'b101),
    .in28(3'b110), .out(multiplexer_1_out), .sel(skrajny_prawo));  // open: in1, in2, in4, in5, in6, in7, in9, in10, in11, in13, in14, in15, in17, in18, in19, in21, in22, in23, in25, in26, in27, in29, in30, in31
  Comparator #(.width(7)) comparator_8 (.a(register_1_q), .b(7'b0100000), .eq(comparator_8_eq));  // open: gt, lt
  assign or_2_out = wsp_x | counter_4_q;  // OR_Gate or_2, 5 bits wide
  Counter #(.max('h1f), .width(5)) counter_10 (
    .count(comparator_7_eq), .Q(counter_10_q), .clk(zegar));  // open: load, D, carry, up, clr
  assign or_3_out = wsp_y | counter_10_q;  // OR_Gate or_3, 5 bits wide
  ROM #(.addrWidth(10), .dataWidth(16)) rom_1 (.addr(counter_1_q), .data(rom_1_data));
  Subtractor #(.width(5)) subtractor_2 (.a(counter_8_q), .b(counter_5_q), .out(subtractor_2_out));  // open: bin, bout
  Subtractor #(.width(5)) subtractor_3 (.a(counter_8_q), .b(counter_6_q), .out(subtractor_3_out));  // open: bin, bout
  Subtractor #(.width(5)) subtractor_4 (.a(counter_8_q), .b(counter_7_q), .out(subtractor_4_out));  // open: bin, bout
  Subtractor #(.width(5)) subtractor_5 (.a(counter_8_q), .b(counter_9_q), .out(subtractor_5_out));  // open: bin, bout
  // RGB_Video #(.height(32), .scale(8), .width(32)) rgb_video_1: pin names not known; wires that end beside it: rgb_video_1_p1, 1'b1, or_2_out, or_3_out, rgb_video_1_p5
  or or_4 (rgb_video_1_p1, zegar, clock_ekran);
  Adder #(.width(5)) adder_9 (.a(subtractor_2_out), .b({5{1'b0}}), .out(adder_9_out));  // open: cin, cout
  Adder #(.width(5)) adder_10 (.a(subtractor_3_out), .b(5'b00001), .out(adder_10_out));  // open: cin, cout
  Adder #(.width(5)) adder_11 (.a(subtractor_4_out), .b(5'b00010), .out(adder_11_out));  // open: cin, cout
  Adder #(.width(5)) adder_12 (.a(subtractor_5_out), .b(5'b00011), .out(adder_12_out));  // open: cin, cout
  Adder #(.width(16)) adder_13 (.a(controlled_buffer_2_out), .b(or_5_out), .out(rgb_video_1_p5));  // open: cin, cout
  assign or_5_out = undriven | rom_1_data;  // OR_Gate or_5, 16 bits wide
  Comparator #(.width(5)) comparator_9 (.a(5'b11010), .b(counter_10_q), .eq(comparator_9_eq));  // open: gt, lt
  Comparator #(.width(5)) comparator_10 (.a(5'b11011), .b(counter_10_q), .eq(comparator_10_eq));  // open: gt, lt
  Comparator #(.width(5)) comparator_11 (.a(5'b11110), .b(counter_10_q), .eq(comparator_11_eq));  // open: gt, lt
  Comparator #(.width(5)) comparator_12 (.a(5'b11101), .b(counter_10_q), .eq(comparator_12_eq));  // open: gt, lt
  Comparator #(.width(5)) comparator_13 (.a({5{1'b1}}), .b(counter_10_q), .eq(comparator_13_eq));  // open: gt, lt
  Comparator #(.width(5)) comparator_14 (.a(5'b11100), .b(counter_10_q), .eq(comparator_14_eq));  // open: gt, lt
  Comparator #(.width(5)) comparator_15 (.a(adder_9_out), .b(counter_4_q), .eq(comparator_15_eq));  // open: gt, lt
  Comparator #(.width(5)) comparator_16 (.a(adder_10_out), .b(counter_4_q), .eq(comparator_16_eq));  // open: gt, lt
  Comparator #(.width(5)) comparator_17 (.a(adder_11_out), .b(counter_4_q), .eq(comparator_17_eq));  // open: gt, lt
  Comparator #(.width(5)) comparator_18 (.a(adder_12_out), .b(counter_4_q), .eq(comparator_18_eq));  // open: gt, lt
  assign controlled_buffer_2_out = not_3_out ? {16{1'b0}} : 16'bz;  // Controlled_Buffer controlled_buffer_2
  assign controlled_buffer_2_out = and_1_out ? 16'hf00a : 16'bz;  // Controlled_Buffer controlled_buffer_3
  not not_3 (not_3_out, and_1_out);
  and and_1 (and_1_out, or_6_out, or_7_out);
  or or_6 (or_6_out, comparator_9_eq, comparator_10_eq, comparator_11_eq, comparator_12_eq, comparator_13_eq, comparator_14_eq);
  or or_7 (or_7_out, comparator_15_eq, comparator_16_eq, comparator_17_eq, comparator_18_eq);
endmodule
