// Logisim project strzal_3klatki_dziala_ponowne_strzelanie (1).circ as structural Verilog: 1 circuit, main circuit main2
module main2 (
  input  [15:0] kolor,
  input  resetowanie,
  input  pierwsza,
  input  kolor_armaty,
  input  [2:0] wybor_miejsca,
  output [15:0] RGB_ekran,
  output [4:0] wspolrzedna_y,
  output clock_ekran,
  output [4:0] wspolrzedna_x,
  output reset_ekran
);

  wire clock_1_out, comparator_9_eq, comparator_10_eq, comparator_11_eq, comparator_12_eq, comparator_13_eq,
       comparator_14_eq, comparator_15_eq, comparator_16_eq, comparator_17_eq, comparator_18_eq,
       comparator_19_eq, comparator_20_eq, comparator_21_eq, comparator_22_eq, comparator_23_eq,
       comparator_24_eq, comparator_25_eq, comparator_26_eq, comparator_27_eq, comparator_28_eq,
       comparator_29_eq, comparator_30_eq, comparator_31_eq, comparator_32_eq, comparator_33_eq, cztery,
       d_ff_1_q, demultiplexer_1_out0, demultiplexer_1_out1, demultiplexer_1_out2, demultiplexer_1_out3,
       demultiplexer_1_out4, demultiplexer_1_out5, demultiplexer_1_out6, demultiplexer_1_out7, dwa, jeden,
       not_1_out, not_2_out, or_2_out, or_3_out, or_4_out, or_5_out, or_6_out, or_7_out, or_8_out, or_9_out,
       osiem, piec, res, siedem, szesc, trzy;
  wire [2:0] counter_2_q, counter_4_q, counter_6_q, counter_8_q, counter_10_q, counter_13_q, counter_14_q,
       counter_16_q;
  wire [9:0] counter_1_q, counter_3_q, counter_5_q, counter_7_q, counter_9_q, counter_11_q, counter_12_q,
       counter_15_q, demultiplexer_2_out0, demultiplexer_2_out1, demultiplexer_2_out2, demultiplexer_3_out0,
       demultiplexer_3_out1, demultiplexer_3_out2, demultiplexer_4_out0, demultiplexer_4_out1,
       demultiplexer_4_out2, demultiplexer_5_out0, demultiplexer_5_out1, demultiplexer_5_out2,
       demultiplexer_6_out0, demultiplexer_6_out1, demultiplexer_6_out2, demultiplexer_7_out0,
       demultiplexer_7_out1, demultiplexer_7_out2, demultiplexer_8_out0, demultiplexer_8_out1,
       demultiplexer_8_out2, demultiplexer_9_out0, demultiplexer_9_out1, demultiplexer_9_out2;
  wire [15:0] controlled_buffer_3_out, klatka1_1_data, klatka1_2_data, klatka2_1_data, klatka2_2_data,
       klatka3_1_data, klatka3_2_data, klatka4_1_data, klatka4_2_data, klatka5_1_data, klatka5_2_data,
       klatka6_1_data, klatka6_2_data, klatka7_1_data, klatka7_2_data, klatka8_1_data, klatka8_2_data,
       multiplexer_1_out, multiplexer_2_out, multiplexer_3_out, multiplexer_4_out, multiplexer_5_out,
       multiplexer_6_out, multiplexer_7_out, multiplexer_8_out, or_10_out, rom_1_data, rom_2_data,
       rom_3_data, rom_4_data, rom_5_data, rom_6_data, rom_7_data, rom_8_data;

  Demultiplexer #(.select(3)) demultiplexer_1 (
    .out0(demultiplexer_1_out0), .out1(demultiplexer_1_out1), .out2(demultiplexer_1_out2),
    .out3(demultiplexer_1_out3), .out4(demultiplexer_1_out4), .out5(demultiplexer_1_out5),
    .out6(demultiplexer_1_out6), .out7(demultiplexer_1_out7), .in(clock_ekran), .sel(wybor_miejsca));
  D_Flip_Flop d_ff_1 (.clk(pierwsza), .D(1'b1), .Q(d_ff_1_q), .reset(res));  // open: Qn, preset
  or or_1 (res, jeden, dwa, trzy, cztery, piec, szesc, siedem, osiem);
  or or_2 (or_2_out, comparator_10_eq, comparator_11_eq, comparator_9_eq);
  or or_3 (or_3_out, comparator_13_eq, comparator_14_eq, comparator_12_eq);
  or or_4 (or_4_out, comparator_16_eq, comparator_17_eq, comparator_15_eq);
  or or_5 (or_5_out, comparator_19_eq, comparator_20_eq, comparator_18_eq);
  or or_6 (or_6_out, comparator_25_eq, comparator_26_eq, comparator_24_eq);
  or or_7 (or_7_out, comparator_28_eq, comparator_29_eq, comparator_27_eq);
  assign clock_ekran = not_1_out ? 1'b0 : 1'bz;  // Controlled_Buffer controlled_buffer_1
  not not_1 (not_1_out, d_ff_1_q);
  Clock clock_1 (.out(clock_1_out));
  Counter #(.max('h3ff), .width(10)) counter_1 (
    .count(demultiplexer_1_out0), .Q(counter_1_q), .clk(demultiplexer_1_out0), .clr(res));  // open: load, D, carry, up
  Counter #(.max('h3), .width(3)) counter_2 (
    .count(or_2_out), .Q(counter_2_q), .clk(demultiplexer_1_out0), .clr(jeden));  // open: load, D, carry, up
  Counter #(.max('h3ff), .width(10)) counter_3 (
    .count(demultiplexer_1_out1), .Q(counter_3_q), .clk(demultiplexer_1_out1), .clr(res));  // open: load, D, carry, up
  Counter #(.max('h3), .width(3)) counter_4 (
    .count(or_3_out), .Q(counter_4_q), .clk(demultiplexer_1_out1), .clr(dwa));  // open: load, D, carry, up
  Counter #(.max('h3ff), .width(10)) counter_5 (
    .count(demultiplexer_1_out2), .Q(counter_5_q), .clk(demultiplexer_1_out2), .clr(res));  // open: load, D, carry, up
  Counter #(.max('h3), .width(3)) counter_6 (
    .count(or_4_out), .Q(counter_6_q), .clk(demultiplexer_1_out2), .clr(trzy));  // open: load, D, carry, up
  Counter #(.max('h3ff), .width(10)) counter_7 (
    .count(demultiplexer_1_out3), .Q(counter_7_q), .clk(demultiplexer_1_out3), .clr(res));  // open: load, D, carry, up
  Counter #(.max('h3), .width(3)) counter_8 (
    .count(or_5_out), .Q(counter_8_q), .clk(demultiplexer_1_out3), .clr(cztery));  // open: load, D, carry, up
  or or_8 (or_8_out, comparator_22_eq, comparator_23_eq, comparator_21_eq);
  Counter #(.max('h3ff), .width(10)) counter_9 (
    .count(demultiplexer_1_out5), .Q(counter_9_q), .clk(demultiplexer_1_out5), .clr(res));  // open: load, D, carry, up
  Counter #(.max('h3), .width(3)) counter_10 (
    .count(or_6_out), .Q(counter_10_q), .clk(demultiplexer_1_out5), .clr(szesc));  // open: load, D, carry, up
  Counter #(.max('h3ff), .width(10)) counter_11 (
    .count(demultiplexer_1_out6), .Q(counter_11_q), .clk(demultiplexer_1_out6), .clr(res));  // open: load, D, carry, up
  or or_9 (or_9_out, comparator_31_eq, comparator_32_eq, comparator_30_eq);
  assign clock_ekran = d_ff_1_q ? clock_1_out : 1'bz;  // Controlled_Buffer controlled_buffer_2
  Comparator #(.width(3)) comparator_1 (.a(counter_2_q), .b(3'b011), .eq(jeden));  // open: gt, lt
  Comparator #(.width(3)) comparator_2 (.a(counter_4_q), .b(3'b011), .eq(dwa));  // open: gt, lt
  Counter #(.max('h3ff), .width(10)) counter_12 (
    .count(demultiplexer_1_out4), .Q(counter_12_q), .clk(demultiplexer_1_out4), .clr(res));  // open: load, D, carry, up
  Counter #(.max('h3), .width(3)) counter_13 (
    .count(or_8_out), .Q(counter_13_q), .clk(demultiplexer_1_out4), .clr(piec));  // open: load, D, carry, up
  Comparator #(.width(3)) comparator_3 (.a(counter_10_q), .b(3'b011), .eq(szesc));  // open: gt, lt
  Counter #(.max('h3), .width(3)) counter_14 (
    .count(or_7_out), .Q(counter_14_q), .clk(demultiplexer_1_out6), .clr(siedem));  // open: load, D, carry, up
  Counter #(.max('h3ff), .width(10)) counter_15 (
    .count(demultiplexer_1_out7), .Q(counter_15_q), .clk(demultiplexer_1_out7), .clr(res));  // open: load, D, carry, up
  Counter #(.max('h3), .width(3)) counter_16 (
    .count(or_9_out), .Q(counter_16_q), .clk(demultiplexer_1_out7), .clr(osiem));  // open: load, D, carry, up
  Comparator #(.width(3)) comparator_4 (.a(counter_6_q), .b(3'b011), .eq(trzy));  // open: gt, lt
  Comparator #(.width(3)) comparator_5 (.a(counter_8_q), .b(3'b011), .eq(cztery));  // open: gt, lt
  Comparator #(.width(3)) comparator_6 (.a(counter_13_q), .b(3'b011), .eq(piec));  // open: gt, lt
  Comparator #(.width(3)) comparator_7 (.a(counter_14_q), .b(3'b011), .eq(siedem));  // open: gt, lt
  Comparator #(.width(3)) comparator_8 (.a(counter_16_q), .b(3'b011), .eq(osiem));  // open: gt, lt
  Demultiplexer #(.select(3), .width(10)) demultiplexer_2 (
    .out0(demultiplexer_2_out0), .out1(demultiplexer_2_out1), .out2(demultiplexer_2_out2), .in(counter_1_q),
    .sel(counter_2_q));  // open: out3, out4, out5, out6, out7
  Demultiplexer #(.select(3), .width(10)) demultiplexer_3 (
    .out0(demultiplexer_3_out0), .out1(demultiplexer_3_out1), .out2(demultiplexer_3_out2), .in(counter_3_q),
    .sel(counter_4_q));  // open: out3, out4, out5, out6, out7
  Demultiplexer #(.select(3), .width(10)) demultiplexer_4 (
    .out0(demultiplexer_4_out0), .out1(demultiplexer_4_out1), .out2(demultiplexer_4_out2), .in(counter_9_q),
    .sel(counter_10_q));  // open: out3, out4, out5, out6, out7
  Counter #(.max('h1f), .width(5)) counter_17 (
    .count(clock_ekran), .Q(wspolrzedna_x), .clk(clock_ekran), .clr(not_1_out));  // open: load, D, carry, up
  Demultiplexer #(.select(3), .width(10)) demultiplexer_5 (
    .out0(demultiplexer_5_out0), .out1(demultiplexer_5_out1), .out2(demultiplexer_5_out2), .in(counter_5_q),
    .sel(counter_6_q));  // open: out3, out4, out5, out6, out7
  Demultiplexer #(.select(3), .width(10)) demultiplexer_6 (
    .out0(demultiplexer_6_out0), .out1(demultiplexer_6_out1), .out2(demultiplexer_6_out2), .in(counter_7_q),
    .sel(counter_8_q));  // open: out3, out4, out5, out6, out7
  Demultiplexer #(.select(3), .width(10)) demultiplexer_7 (
    .out0(demultiplexer_7_out0), .out1(demultiplexer_7_out1), .out2(demultiplexer_7_out2), .in(counter_12_q),
    .sel(counter_13_q));  // open: out3, out4, out5, out6, out7
  Demultiplexer #(.select(3), .width(10)) demultiplexer_8 (
    .out0(demultiplexer_8_out0), .out1(demultiplexer_8_out1), .out2(demultiplexer_8_out2), .in(counter_11_q),
    .sel(counter_14_q));  // open: out3, out4, out5, out6, out7
  Demultiplexer #(.select(3), .width(10)) demultiplexer_9 (
    .out0(demultiplexer_9_out0), .out1(demultiplexer_9_out1), .out2(demultiplexer_9_out2), .in(counter_15_q),
    .sel(counter_16_q));  // open: out3, out4, out5, out6, out7
  ROM #(.addrWidth(10), .dataWidth(16)) klatka1_1 (.addr(demultiplexer_2_out0), .data(klatka1_1_data));
  ROM #(.addrWidth(10), .dataWidth(16)) klatka1_2 (.addr(demultiplexer_2_out1), .data(klatka1_2_data));
  ROM #(.addrWidth(10), .dataWidth(16)) rom_1 (.addr(demultiplexer_2_out2), .data(rom_1_data));
  Comparator #(.width(10)) comparator_9 (.a(demultiplexer_2_out0), .b(10'h3e8), .eq(comparator_9_eq));  // open: gt, lt
  Comparator #(.width(10)) comparator_10 (
    .a(demultiplexer_2_out1), .b(10'h3e8), .eq(comparator_10_eq));  // open: gt, lt
  Comparator #(.width(10)) comparator_11 (
    .a(demultiplexer_2_out2), .b(10'h3e8), .eq(comparator_11_eq));  // open: gt, lt
  ROM #(.addrWidth(10), .dataWidth(16)) klatka2_1 (.addr(demultiplexer_3_out0), .data(klatka2_1_data));
  ROM #(.addrWidth(10), .dataWidth(16)) klatka2_2 (.addr(demultiplexer_3_out1), .data(klatka2_2_data));
  ROM #(.addrWidth(10), .dataWidth(16)) rom_2 (.addr(demultiplexer_3_out2), .data(rom_2_data));
  Comparator #(.width(10)) comparator_12 (
    .a(demultiplexer_3_out0), .b(10'h3e8), .eq(comparator_12_eq));  // open: gt, lt
  Comparator #(.width(10)) comparator_13 (
    .a(demultiplexer_3_out1), .b(10'h3e8), .eq(comparator_13_eq));  // open: gt, lt
  Comparator #(.width(10)) comparator_14 (
    .a(demultiplexer_3_out2), .b(10'h3e8), .eq(comparator_14_eq));  // open: gt, lt
  ROM #(.addrWidth(10), .dataWidth(16), .misaligned("true")) klatka3_1 (
    .addr(demultiplexer_5_out0), .data(klatka3_1_data));
  ROM #(.addrWidth(10), .dataWidth(16)) klatka3_2 (.addr(demultiplexer_5_out1), .data(klatka3_2_data));
  Comparator #(.width(10)) comparator_15 (
    .a(demultiplexer_5_out0), .b(10'h3e8), .eq(comparator_15_eq));  // open: gt, lt
  Comparator #(.width(10)) comparator_16 (
    .a(demultiplexer_5_out1), .b(10'h3e8), .eq(comparator_16_eq));  // open: gt, lt
  Comparator #(.width(10)) comparator_17 (
    .a(demultiplexer_5_out2), .b(10'h3e8), .eq(comparator_17_eq));  // open: gt, lt
  Comparator #(.width(10)) comparator_18 (
    .a(demultiplexer_6_out0), .b(10'h3e8), .eq(comparator_18_eq));  // open: gt, lt
  Comparator #(.width(10)) comparator_19 (
    .a(demultiplexer_6_out1), .b(10'h3e8), .eq(comparator_19_eq));  // open: gt, lt
  Comparator #(.width(10)) comparator_20 (
    .a(demultiplexer_6_out2), .b(10'h3e8), .eq(comparator_20_eq));  // open: gt, lt
  Comparator #(.width(10)) comparator_21 (
    .a(demultiplexer_7_out0), .b(10'h3e8), .eq(comparator_21_eq));  // open: gt, lt
  Comparator #(.width(10)) comparator_22 (
    .a(demultiplexer_7_out1), .b(10'h3e8), .eq(comparator_22_eq));  // open: gt, lt
  Comparator #(.width(10)) comparator_23 (
    .a(demultiplexer_7_out2), .b(10'h3e8), .eq(comparator_23_eq));  // open: gt, lt
  ROM #(.addrWidth(10), .dataWidth(16)) klatka6_1 (.addr(demultiplexer_4_out0), .data(klatka6_1_data));
  ROM #(.addrWidth(10), .dataWidth(16)) klatka6_2 (.addr(demultiplexer_4_out1), .data(klatka6_2_data));
  ROM #(.addrWidth(10), .dataWidth(16)) rom_3 (.addr(demultiplexer_4_out2), .data(rom_3_data));
  Comparator #(.width(10)) comparator_24 (
    .a(demultiplexer_4_out0), .b(10'h3e8), .eq(comparator_24_eq));  // open: gt, lt
  Comparator #(.width(10)) comparator_25 (
    .a(demultiplexer_4_out1), .b(10'h3e8), .eq(comparator_25_eq));  // open: gt, lt
  Comparator #(.width(10)) comparator_26 (
    .a(demultiplexer_4_out2), .b(10'h3e8), .eq(comparator_26_eq));  // open: gt, lt
  Comparator #(.width(10)) comparator_27 (
    .a(demultiplexer_8_out0), .b(10'h3e8), .eq(comparator_27_eq));  // open: gt, lt
  Comparator #(.width(10)) comparator_28 (
    .a(demultiplexer_8_out1), .b(10'h3e8), .eq(comparator_28_eq));  // open: gt, lt
  Comparator #(.width(10)) comparator_29 (
    .a(demultiplexer_8_out2), .b(10'h3e8), .eq(comparator_29_eq));  // open: gt, lt
  Comparator #(.width(10)) comparator_30 (
    .a(demultiplexer_9_out0), .b(10'h3e8), .eq(comparator_30_eq));  // open: gt, lt
  Comparator #(.width(10)) comparator_31 (
    .a(demultiplexer_9_out1), .b(10'h3e8), .eq(comparator_31_eq));  // open: gt, lt
  Comparator #(.width(10)) comparator_32 (
    .a(demultiplexer_9_out2), .b(10'h3e8), .eq(comparator_32_eq));  // open: gt, lt
  ROM #(.addrWidth(10), .dataWidth(16)) rom_4 (.addr(demultiplexer_5_out2), .data(rom_4_data));
  ROM #(.addrWidth(10), .dataWidth(16)) klatka4_1 (.addr(demultiplexer_6_out0), .data(klatka4_1_data));
  ROM #(.addrWidth(10), .dataWidth(16)) klatka4_2 (.addr(demultiplexer_6_out1), .data(klatka4_2_data));
  ROM #(.addrWidth(10), .dataWidth(16)) rom_5 (.addr(demultiplexer_6_out2), .data(rom_5_data));
  ROM #(.addrWidth(10), .dataWidth(16)) klatka5_1 (.addr(demultiplexer_7_out0), .data(klatka5_1_data));
  ROM #(.addrWidth(10), .dataWidth(16)) klatka5_2 (.addr(demultiplexer_7_out1), .data(klatka5_2_data));
  ROM #(.addrWidth(10), .dataWidth(16)) rom_6 (.addr(demultiplexer_7_out2), .data(rom_6_data));
  ROM #(.addrWidth(10), .dataWidth(16)) klatka7_1 (.addr(demultiplexer_8_out0), .data(klatka7_1_data));
  ROM #(.addrWidth(10), .dataWidth(16)) klatka7_2 (.addr(demultiplexer_8_out1), .data(klatka7_2_data));
  ROM #(.addrWidth(10), .dataWidth(16)) rom_7 (.addr(demultiplexer_8_out2), .data(rom_7_data));
  ROM #(.addrWidth(10), .dataWidth(16)) klatka8_1 (.addr(demultiplexer_9_out0), .data(klatka8_1_data));
  ROM #(.addrWidth(10), .dataWidth(16)) klatka8_2 (.addr(demultiplexer_9_out1), .data(klatka8_2_data));
  ROM #(.addrWidth(10), .dataWidth(16)) rom_8 (.addr(demultiplexer_9_out2), .data(rom_8_data));
  Comparator #(.width(5)) comparator_33 (.a(wspolrzedna_x), .b({5{1'b1}}), .eq(comparator_33_eq));  // open: gt, lt
  Counter #(.max('h1f), .width(5)) counter_18 (
    .count(comparator_33_eq), .Q(wspolrzedna_y), .clk(clock_ekran), .clr(not_1_out));  // open: load, D, carry, up
  // RGB_Video #(.height(32), .scale(8), .width(32)) rgb_video_1: pin names not known; wires that end beside it: resetowanie, clock_ekran, 1'b1, wspolrzedna_x, wspolrzedna_y, RGB_ekran
  Multiplexer #(.select(3), .width(16)) multiplexer_1 (
    .in0(klatka1_1_data), .in1(klatka1_2_data), .in2(rom_1_data), .out(multiplexer_1_out), .sel(counter_2_q));  // open: in3, in4, in5, in6, in7
  Multiplexer #(.select(3), .width(16)) multiplexer_2 (
    .in0(klatka6_1_data), .in1(klatka6_2_data), .in2(rom_3_data), .out(multiplexer_2_out), .sel(counter_10_q));  // open: in3, in4, in5, in6, in7
  Multiplexer #(.select(3), .width(16)) multiplexer_3 (
    .in0(klatka2_1_data), .in1(klatka2_2_data), .in2(rom_2_data), .out(multiplexer_3_out), .sel(counter_4_q));  // open: in3, in4, in5, in6, in7
  Multiplexer #(.select(3), .width(16)) multiplexer_4 (
    .in0(klatka3_1_data), .in1(klatka3_2_data), .in2(rom_4_data), .out(multiplexer_4_out), .sel(counter_6_q));  // open: in3, in4, in5, in6, in7
  Multiplexer #(.select(3), .width(16)) multiplexer_5 (
    .in0(klatka4_1_data), .in1(klatka4_2_data), .in2(rom_5_data), .out(multiplexer_5_out), .sel(counter_8_q));  // open: in3, in4, in5, in6, in7
  Multiplexer #(.select(3), .width(16)) multiplexer_6 (
    .in0(klatka5_1_data), .in1(klatka5_2_data), .in2(rom_6_data), .out(multiplexer_6_out), .sel(counter_13_q));  // open: in3, in4, in5, in6, in7
  Multiplexer #(.select(3), .width(16)) multiplexer_7 (
    .in0(klatka7_1_data), .in1(klatka7_2_data), .in2(rom_7_data), .out(multiplexer_7_out), .sel(counter_14_q));  // open: in3, in4, in5, in6, in7
  Multiplexer #(.select(3), .width(16)) multiplexer_8 (
    .in0(klatka8_1_data), .in1(klatka8_2_data), .in2(rom_8_data), .out(multiplexer_8_out), .sel(counter_16_q));  // open: in3, in4, in5, in6, in7
  Adder #(.width(16)) adder_1 (.a(controlled_buffer_3_out), .b(or_10_out), .out(RGB_ekran));  // open: cin, cout
  assign or_10_out = multiplexer_1_out | multiplexer_3_out | multiplexer_4_out | multiplexer_5_out | multiplexer_6_out | multiplexer_2_out | multiplexer_7_out | multiplexer_8_out;  // OR_Gate or_10, 16 bits wide
  assign controlled_buffer_3_out = not_2_out ? {16{1'b0}} : 16'bz;  // Controlled_Buffer controlled_buffer_3
  assign controlled_buffer_3_out = kolor_armaty ? kolor : 16'bz;  // Controlled_Buffer controlled_buffer_4
  not not_2 (not_2_out, kolor_armaty);

  assign reset_ekran = resetowanie;

  // Notes on the sheet:
  //   contents of klatka1_1 (hex, n*v repeats v):
  //   0 7fff 7fff 30*0 7fff 7fff 30*0 7fff 7fff 30*0 7fff 7fff 30*0 7fff 7fff 30*0 7fff 7fff 30*0 7fff
  //   7fff 30*0 7fff 7fff 30*0 7fff 7fff 30*0 7fff 7fff 30*0 7fff 7fff 30*0 7fff 7fff 30*0 7fff 7fff 30*0
  //   7fff 7fff 30*0 7fff 7fff 30*0 7fff 7fff 30*0 7fff 7fff 30*0 7fff 7fff 30*0 7fff 7fff 30*0 7fff 7fff
  //   30*0 7fff 7fff 30*0 7fff 7fff 30*0 7fff 7fff 30*0 7fff 7fff 30*0 7fff 7fff 30*0 7fff 7fff 30*0 7fff
  //   7fff 30*0 7fff 7fff 30*0 7fff 7fff
  //   contents of klatka1_2 (hex, n*v repeats v):
  //   4*6318 28*0 6318 7fff 7fff 7fff 28*0 6318 7fff 7fff 7fff 28*0 7fff 7fff 7fff 6318 6318 27*0 7fff
  //   7fff 7fff 6318 6318 27*0 7fff 7fff 6318 6318 6318 27*0 7fff 6318 6318 7fff 28*0 6318 6318 7fff 7fff
  //   28*0 4*7fff 28*0 7fff 7fff 7fff 6318 28*0 7fff 7fff 7fff 6318 6318 27*0 7fff 7fff 6318 6318 6318
  //   27*0 7fff 6318 6318 7fff 28*0 6318 6318 7fff 7fff 28*0 6318 6318 7fff 7fff 28*0 4*7fff 28*0 4*7fff
  //   6318 27*0 7fff 7fff 7fff 6318 6318 27*0 7fff 7fff 6318 6318 6318 27*0 7fff 6318 6318 7fff 28*0 6318
  //   6318 7fff 7fff 28*0 6318 7fff 7fff 7fff 6318 27*0 6318 7fff 7fff 7fff 0 6318 26*0 7fff 7fff 7fff
  //   6318 6318 27*0 7fff 7fff 6318 6318 28*0 7fff 6318 6318 7fff 28*0 6318 6318 7fff 7fff 28*0 4*7fff
  //   155*0 1
  //   contents of klatka2_1 (hex, n*v repeats v):
  //   5*0 7fff 7fff 30*0 7fff 7fff 30*0 7fff 7fff 30*0 7fff 7fff 30*0 7fff 7fff 30*0 7fff 7fff 30*0 7fff
  //   7fff 30*0 7fff 7fff 30*0 7fff 7fff 30*0 7fff 7fff 30*0 7fff 7fff 30*0 7fff 7fff 30*0 7fff 7fff 30*0
  //   7fff 7fff 30*0 7fff 7fff 30*0 7fff 7fff 30*0 7fff 7fff 30*0 7fff 7fff 30*0 7fff 7fff 30*0 7fff 7fff
  //   30*0 7fff 7fff 30*0 7fff 7fff 30*0 7fff 7fff 30*0 7fff 7fff 30*0 7fff 7fff 30*0 7fff 7fff 30*0 7fff
  //   7fff 30*0 7fff 7fff
  //   contents of klatka2_2 (hex, n*v repeats v):
  //   4*0 4*6318 28*0 6318 7fff 7fff 7fff 28*0 6318 7fff 7fff 7fff 28*0 7fff 7fff 7fff 6318 6318 27*0 7fff
  //   7fff 7fff 6318 6318 27*0 7fff 7fff 6318 6318 6318 26*0 6318 7fff 6318 6318 7fff 26*0 6318 0 6318
  //   6318 7fff 7fff 27*0 6318 4*7fff 27*0 6318 7fff 7fff 7fff 6318 28*0 7fff 7fff 7fff 6318 6318 27*0
  //   7fff 7fff 6318 6318 6318 27*0 7fff 6318 6318 7fff 28*0 6318 6318 7fff 7fff 27*0 6318 6318 6318 7fff
  //   7fff 27*0 6318 4*7fff 28*0 4*7fff 6318 27*0 7fff 7fff 7fff 6318 6318 27*0 7fff 7fff 6318 6318 6318
  //   27*0 7fff 6318 6318 7fff 28*0 6318 6318 7fff 7fff 27*0 6318 6318 7fff 7fff 7fff 6318 26*0 6318 6318
  //   7fff 7fff 7fff 0 6318 26*0 7fff 7fff 7fff 6318 6318 27*0 7fff 7fff 6318 6318 28*0 7fff 6318 6318
  //   7fff 27*0 6318 6318 6318 7fff 7fff 28*0 4*7fff
  //   contents of klatka3_1 (hex, n*v repeats v):
  //   9*0 7fff 7fff 30*0 7fff 7fff 30*0 7fff 7fff 30*0 7fff 7fff 30*0 7fff 7fff 30*0 7fff 7fff 30*0 7fff
  //   7fff 30*0 7fff 7fff 30*0 7fff 7fff 30*0 7fff 7fff 30*0 7fff 7fff 30*0 7fff 7fff 30*0 7fff 7fff 30*0
  //   7fff 7fff 30*0 7fff 7fff 30*0 7fff 7fff 30*0 7fff 7fff 30*0 7fff 7fff 30*0 7fff 7fff 30*0 7fff 7fff
  //   30*0 7fff 7fff 30*0 7fff 7fff 30*0 7fff 7fff 30*0 7fff 7fff 30*0 7fff 7fff 30*0 7fff 7fff 30*0 7fff
  //   7fff 30*0 7fff 7fff
  //   contents of klatka3_2 (hex, n*v repeats v):
  //   8*0 4*6318 28*0 6318 7fff 7fff 7fff 28*0 6318 7fff 7fff 7fff 28*0 7fff 7fff 7fff 6318 6318 27*0 7fff
  //   7fff 7fff 6318 6318 27*0 7fff 7fff 6318 6318 6318 26*0 6318 7fff 6318 6318 7fff 26*0 6318 0 6318
  //   6318 7fff 7fff 27*0 6318 4*7fff 27*0 6318 7fff 7fff 7fff 6318 28*0 7fff 7fff 7fff 6318 6318 27*0
  //   7fff 7fff 6318 6318 6318 27*0 7fff 6318 6318 7fff 28*0 6318 6318 7fff 7fff 27*0 6318 6318 6318 7fff
  //   7fff 27*0 6318 4*7fff 28*0 4*7fff 6318 27*0 7fff 7fff 7fff 6318 6318 27*0 7fff 7fff 6318 6318 6318
  //   27*0 7fff 6318 6318 7fff 28*0 6318 6318 7fff 7fff 27*0 6318 6318 7fff 7fff 7fff 6318 26*0 6318 6318
  //   7fff 7fff 7fff 0 6318 26*0 7fff 7fff 7fff 6318 6318 27*0 7fff 7fff 6318 6318 28*0 7fff 6318 6318
  //   7fff 27*0 6318 6318 6318 7fff 7fff 28*0 4*7fff
  //   contents of klatka6_1 (hex, n*v repeats v):
  //   21*0 7fff 7fff 30*0 7fff 7fff 30*0 7fff 7fff 30*0 7fff 7fff 30*0 7fff 7fff 30*0 7fff 7fff 30*0 7fff
  //   7fff 30*0 7fff 7fff 30*0 7fff 7fff 30*0 7fff 7fff 30*0 7fff 7fff 30*0 7fff 7fff 30*0 7fff 7fff 30*0
  //   7fff 7fff 30*0 7fff 7fff 30*0 7fff 7fff 30*0 7fff 7fff 30*0 7fff 7fff 30*0 7fff 7fff 30*0 7fff 7fff
  //   30*0 7fff 7fff 30*0 7fff 7fff 30*0 7fff 7fff 30*0 7fff 7fff 30*0 7fff 7fff 30*0 7fff 7fff 30*0 7fff
  //   7fff 30*0 7fff 7fff
  //   contents of klatka6_2 (hex, n*v repeats v):
  //   20*0 4*6318 28*0 6318 7fff 7fff 7fff 28*0 6318 7fff 7fff 7fff 28*0 7fff 7fff 7fff 6318 6318 27*0
  //   7fff 7fff 7fff 6318 6318 27*0 7fff 7fff 6318 6318 6318 26*0 6318 7fff 6318 6318 7fff 26*0 6318 0
  //   6318 6318 7fff 7fff 27*0 6318 4*7fff 27*0 6318 7fff 7fff 7fff 6318 28*0 7fff 7fff 7fff 6318 6318
  //   27*0 7fff 7fff 6318 6318 6318 27*0 7fff 6318 6318 7fff 28*0 6318 6318 7fff 7fff 27*0 6318 6318 6318
  //   7fff 7fff 27*0 6318 4*7fff 28*0 4*7fff 6318 27*0 7fff 7fff 7fff 6318 6318 27*0 7fff 7fff 6318 6318
  //   6318 27*0 7fff 6318 6318 7fff 28*0 6318 6318 7fff 7fff 27*0 6318 6318 7fff 7fff 7fff 6318 26*0 6318
  //   6318 7fff 7fff 7fff 0 6318 26*0 7fff 7fff 7fff 6318 6318 27*0 7fff 7fff 6318 6318 28*0 7fff 6318
  //   6318 7fff 27*0 6318 6318 6318 7fff 7fff 28*0 4*7fff
  //   contents of klatka4_1 (hex, n*v repeats v):
  //   13*0 7fff 7fff 30*0 7fff 7fff 30*0 7fff 7fff 30*0 7fff 7fff 30*0 7fff 7fff 30*0 7fff 7fff 30*0 7fff
  //   7fff 30*0 7fff 7fff 30*0 7fff 7fff 30*0 7fff 7fff 30*0 7fff 7fff 30*0 7fff 7fff 30*0 7fff 7fff 30*0
  //   7fff 7fff 30*0 7fff 7fff 30*0 7fff 7fff 30*0 7fff 7fff 30*0 7fff 7fff 30*0 7fff 7fff 30*0 7fff 7fff
  //   30*0 7fff 7fff 30*0 7fff 7fff 30*0 7fff 7fff 30*0 7fff 7fff 30*0 7fff 7fff 30*0 7fff 7fff 30*0 7fff
  //   7fff 30*0 7fff 7fff
  //   contents of klatka4_2 (hex, n*v repeats v):
  //   12*0 4*6318 28*0 6318 7fff 7fff 7fff 28*0 6318 7fff 7fff 7fff 28*0 7fff 7fff 7fff 6318 6318 27*0
  //   7fff 7fff 7fff 6318 6318 27*0 7fff 7fff 6318 6318 6318 26*0 6318 7fff 6318 6318 7fff 26*0 6318 0
  //   6318 6318 7fff 7fff 27*0 6318 4*7fff 27*0 6318 7fff 7fff 7fff 6318 28*0 7fff 7fff 7fff 6318 6318
  //   27*0 7fff 7fff 6318 6318 6318 27*0 7fff 6318 6318 7fff 28*0 6318 6318 7fff 7fff 27*0 6318 6318 6318
  //   7fff 7fff 27*0 6318 4*7fff 28*0 4*7fff 6318 27*0 7fff 7fff 7fff 6318 6318 27*0 7fff 7fff 6318 6318
  //   6318 27*0 7fff 6318 6318 7fff 28*0 6318 6318 7fff 7fff 27*0 6318 6318 7fff 7fff 7fff 6318 26*0 6318
  //   6318 7fff 7fff 7fff 0 6318 26*0 7fff 7fff 7fff 6318 6318 27*0 7fff 7fff 6318 6318 28*0 7fff 6318
  //   6318 7fff 27*0 6318 6318 6318 7fff 7fff 28*0 4*7fff
  //   contents of klatka5_1 (hex, n*v repeats v):
  //   17*0 7fff 7fff 30*0 7fff 7fff 30*0 7fff 7fff 30*0 7fff 7fff 30*0 7fff 7fff 30*0 7fff 7fff 30*0 7fff
  //   7fff 30*0 7fff 7fff 30*0 7fff 7fff 30*0 7fff 7fff 30*0 7fff 7fff 30*0 7fff 7fff 30*0 7fff 7fff 30*0
  //   7fff 7fff 30*0 7fff 7fff 30*0 7fff 7fff 30*0 7fff 7fff 30*0 7fff 7fff 30*0 7fff 7fff 30*0 7fff 7fff
  //   30*0 7fff 7fff 30*0 7fff 7fff 30*0 7fff 7fff 30*0 7fff 7fff 30*0 7fff 7fff 30*0 7fff 7fff 30*0 7fff
  //   7fff 30*0 7fff 7fff
  //   contents of klatka5_2 (hex, n*v repeats v):
  //   48*0 4*6318 28*0 6318 7fff 7fff 7fff 28*0 6318 7fff 7fff 7fff 28*0 7fff 7fff 7fff 6318 6318 27*0
  //   7fff 7fff 7fff 6318 6318 27*0 7fff 7fff 6318 6318 6318 26*0 6318 7fff 6318 6318 7fff 26*0 6318 0
  //   6318 6318 7fff 7fff 27*0 6318 4*7fff 27*0 6318 7fff 7fff 7fff 6318 28*0 7fff 7fff 7fff 6318 6318
  //   27*0 7fff 7fff 6318 6318 6318 27*0 7fff 6318 6318 7fff 28*0 6318 6318 7fff 7fff 27*0 6318 6318 6318
  //   7fff 7fff 27*0 6318 4*7fff 28*0 4*7fff 6318 27*0 7fff 7fff 7fff 6318 6318 27*0 7fff 7fff 6318 6318
  //   6318 27*0 7fff 6318 6318 7fff 28*0 6318 6318 7fff 7fff 27*0 6318 6318 7fff 7fff 7fff 6318 26*0 6318
  //   6318 7fff 7fff 7fff 0 6318 26*0 7fff 7fff 7fff 6318 6318 27*0 7fff 7fff 6318 6318 28*0 7fff 6318
  //   6318 7fff 27*0 6318 6318 6318 7fff 7fff 28*0 4*7fff
  //   contents of klatka7_1 (hex, n*v repeats v):
  //   25*0 7fff 7fff 30*0 7fff 7fff 30*0 7fff 7fff 30*0 7fff 7fff 30*0 7fff 7fff 30*0 7fff 7fff 30*0 7fff
  //   7fff 30*0 7fff 7fff 30*0 7fff 7fff 30*0 7fff 7fff 30*0 7fff 7fff 30*0 7fff 7fff 30*0 7fff 7fff 30*0
  //   7fff 7fff 30*0 7fff 7fff 30*0 7fff 7fff 30*0 7fff 7fff 30*0 7fff 7fff 30*0 7fff 7fff 30*0 7fff 7fff
  //   30*0 7fff 7fff 30*0 7fff 7fff 30*0 7fff 7fff 30*0 7fff 7fff 30*0 7fff 7fff 30*0 7fff 7fff 30*0 7fff
  //   7fff 30*0 7fff 7fff
  //   contents of klatka7_2 (hex, n*v repeats v):
  //   24*0 4*6318 28*0 6318 7fff 7fff 7fff 28*0 6318 7fff 7fff 7fff 28*0 7fff 7fff 7fff 6318 6318 27*0
  //   7fff 7fff 7fff 6318 6318 27*0 7fff 7fff 6318 6318 6318 26*0 6318 7fff 6318 6318 7fff 26*0 6318 0
  //   6318 6318 7fff 7fff 27*0 6318 4*7fff 27*0 6318 7fff 7fff 7fff 6318 28*0 7fff 7fff 7fff 6318 6318
  //   27*0 7fff 7fff 6318 6318 6318 27*0 7fff 6318 6318 7fff 28*0 6318 6318 7fff 7fff 27*0 6318 6318 6318
  //   7fff 7fff 27*0 6318 4*7fff 28*0 4*7fff 6318 27*0 7fff 7fff 7fff 6318 6318 27*0 7fff 7fff 6318 6318
  //   6318 27*0 7fff 6318 6318 7fff 28*0 6318 6318 7fff 7fff 27*0 6318 6318 7fff 7fff 7fff 6318 26*0 6318
  //   6318 7fff 7fff 7fff 0 6318 26*0 7fff 7fff 7fff 6318 6318 27*0 7fff 7fff 6318 6318 28*0 7fff 6318
  //   6318 7fff 27*0 6318 6318 6318 7fff 7fff 28*0 4*7fff
  //   contents of klatka8_1 (hex, n*v repeats v):
  //   29*0 7fff 7fff 30*0 7fff 7fff 30*0 7fff 7fff 30*0 7fff 7fff 30*0 7fff 7fff 30*0 7fff 7fff 30*0 7fff
  //   7fff 30*0 7fff 7fff 30*0 7fff 7fff 30*0 7fff 7fff 30*0 7fff 7fff 30*0 7fff 7fff 30*0 7fff 7fff 30*0
  //   7fff 7fff 30*0 7fff 7fff 30*0 7fff 7fff 30*0 7fff 7fff 30*0 7fff 7fff 30*0 7fff 7fff 30*0 7fff 7fff
  //   30*0 7fff 7fff 30*0 7fff 7fff 30*0 7fff 7fff 30*0 7fff 7fff 30*0 7fff 7fff 30*0 7fff 7fff 30*0 7fff
  //   7fff 30*0 7fff 7fff
  //   contents of klatka8_2 (hex, n*v repeats v):
  //   28*0 4*6318 28*0 6318 7fff 7fff 7fff 28*0 6318 7fff 7fff 7fff 28*0 7fff 7fff 7fff 6318 28*0 7fff
  //   7fff 7fff 6318 28*0 7fff 7fff 6318 6318 27*0 6318 7fff 6318 6318 7fff 26*0 6318 0 6318 6318 7fff
  //   7fff 27*0 6318 4*7fff 27*0 6318 7fff 7fff 7fff 6318 28*0 7fff 7fff 7fff 6318 28*0 7fff 7fff 6318
  //   6318 28*0 7fff 6318 6318 7fff 28*0 6318 6318 7fff 7fff 27*0 6318 6318 6318 7fff 7fff 27*0 6318
  //   4*7fff 28*0 4*7fff 28*0 7fff 7fff 7fff 6318 28*0 7fff 7fff 6318 6318 28*0 7fff 6318 6318 7fff 28*0
  //   6318 6318 7fff 7fff 27*0 6318 6318 7fff 7fff 7fff 27*0 6318 6318 7fff 7fff 7fff 28*0 7fff 7fff 7fff
  //   6318 28*0 7fff 7fff 6318 6318 28*0 7fff 6318 6318 7fff 27*0 6318 6318 6318 7fff 7fff 28*0 4*7fff
endmodule
